// Logisim project hrmcpu.circ as structural Verilog: 10 circuits, main circuit TOP
module TOP (
);

  wire alu_1_flag, branch, clock_1_out, empty, fb, full, ijump, muxM, rIN, rst, rstPC, srcA, undriven, wIR,
       wM, wO, wPC, wR;
  wire [1:0] muxR;
  wire [2:0] aluCtl;
  wire [7:0] alu_1_aluout, inbox_1_din, INSTR, memory_1_m, pc_1_pc, prog_1_data, r_1_r;

  // Probe on prog_1_data
  PROG prog_1 (.Addr(pc_1_pc), .Data(prog_1_data));
  // Probe on INSTR
  IR ir_1 (.nIR(prog_1_data), .wIR(wIR), .rIR(INSTR));
  // Probe on inbox_1_din
  INBOX inbox_1 (.rIn(rIN), .rst(rst), .empty(empty), .DIN(inbox_1_din));
  LED lEmpty (.in(empty));
  // Probe on r_1_r
  R r_1 (.iInbox(inbox_1_din), .iMem(memory_1_m), .iAlu(alu_1_aluout), .muxR(muxR), .wR(wR), .R(r_1_r));
  // Probe on memory_1_m
  MEMORY memory_1 (
    .ADDR(prog_1_data), .srcA(srcA), .wM(wM), .R(r_1_r), .aluOut(alu_1_aluout), .muxM(muxM), .fb(fb),
    .M(memory_1_m));
  PC pc_1 (
    .branch(branch), .ijump(ijump), .aluFlag(alu_1_flag), .jmpAddr(prog_1_data), .wPC(wPC), .rst(rstPC),
    .PC(pc_1_pc));
  ALU alu_1 (.inR(r_1_r), .inM(memory_1_m), .aluCtl(aluCtl), .flag(alu_1_flag), .aluOut(alu_1_aluout));
  // Probe on alu_1_aluout
  // Probe on pc_1_pc
  OUTBOX outbox_1 (.DOUT(r_1_r), .wO(wO), .full(full));
  Clock clock_1 (.out(clock_1_out));
  // FSM_Entity #(.content("fsm ControlUnit @[ 34 , 30 , 1400 , 800 ]\n{ in INSTR [ 8 ] @[ 34 , 100 , 68 , 15 ]\n;\nin inEmpty [ 1 ] @[ 34 , 140 , 53 , 15 ]\n;\nin outFull [ 1 ] @[ 34 , 178 , 45 , 15 ]\n;\nout wIR [ 1 ] @[ 1408 , 93 , 26 , 15 ]\n;\nout muxR [ 2 ] @[ 1368 , 150 , 66 , 15 ]\n;\nout wR [ 1 ] @[ 1411 , 177 , 23 , 15 ]\n;\nout muxM [ 1 ] @[ 1393 , 222 , 41 , 15 ]\n;\nout srcA [ 1 ] @[ 1402 , 244 , 32 , 15 ]\n;\nout wM [ 1 ] @[ 1409 , 268 , 25 , 15 ]\n;\nout fb [ 1 ] @[ 1416 , 303 , 18 , 15 ]\n;\nout aluCtl [ 3 ] @[ 1367 , 333 , 67 , 15 ]\n;\nout wPC [ 1 ] @[ 1403 , 366 , 31 , 15 ]\n;\nout rIn [ 1 ] @[ 1412 , 390 , 22 , 15 ]\n;\nout wO [ 1 ] @[ 1409 , 415 , 25 , 15 ]\n;\nout ijump [ 1 ] @[ 1395 , 467 , 39 , 15 ]\n;\nout branch [ 1 ] @[ 1387 , 490 , 47 , 15 ]\n;\nout rst [ 1 ] @[ 1411 , 523 , 23 , 15 ]\n;\nout halt [ 1 ] @[ 1406 , 553 , 28 , 15 ]\n;\ncodeWidth = 6 ; reset = RESET ; state RESET = \"000000\" @[ 116 , 74 , 30 , 30 ]\n{\ncommands @[ 161 , 89 , 52 , 21 ]\n{\nrst = \"1\" ;\n}\ntransitions {\nRESET -> FETCH_I when default @[ 280 , 79 , 47 , 21 ]\n;\n}\n}\nstate Inc_PC = \"000010\" @[ 187 , 148 , 30 , 30 ]\n{\ncommands @[ 241 , 155 , 61 , 21 ]\n{\nwPC = \"1\" ;\n}\ntransitions {\nInc_PC -> FETCH_I when default @[ 279 , 123 , 47 , 21 ]\n;\n}\n}\nstate FETCH_I = \"000100\" @[ 418 , 75 , 30 , 30 ]\n{\ncommands @[ 484 , 83 , 55 , 21 ]\n{\nwIR = \"0\" ;\n}\ntransitions {\nFETCH_I -> LOAD_IR when default @[ 388 , 132 , 47 , 21 ]\n;\n}\n}\nstate INBOX1 = \"000110\" @[ 343 , 498 , 30 , 30 ]\n{\ncommands @[ 389 , 511 , 51 , 21 ]\n{\nrIn = \"1\" ;\n}\ntransitions {\nINBOX1 -> INBOX2 when default @[ 330 , 563 , 47 , 21 ]\n;\n}\n}\nstate INBOX2 = \"001000\" @[ 336 , 595 , 30 , 30 ]\n{\ncommands @[ 382 , 608 , 75 , 36 ]\n{\nmuxR = \"00\" ;\nwR = \"1\" ;\n}\ntransitions {\nINBOX2 -> Inc_PC when default @[ 37 , 448 , 47 , 21 ]\n;\n}\n}\nstate OUTBOX = \"001010\" @[ 134 , 446 , 30 , 30 ]\n{\ncommands @[ 179 , 461 , 54 , 21 ]\n{\nwO = \"1\" ;\n}\ntransitions {\nOUTBOX -> Inc_PC when default @[ 55 , 330 , 47 , 21 ]\n;\n}\n}\nstate INCPC2 = \"001100\" @[ 652 , 208 , 30 , 30 ]\n{\ncommands @[ 707 , 214 , 61 , 21 ]\n{\nwPC = \"1\" ;\n}\ntransitions {\nINCPC2 -> FETCH_O when default @[ 665 , 268 , 47 , 21 ]\n;\n}\n}\nstate READMEM = \"001110\" @[ 652 , 407 , 30 , 30 ]\n{\ncommands @[ 711 , 421 , 62 , 21 ]\n{\nsrcA = \"0\" ;\n}\ntransitions {\nREADMEM -> BUMPP when INSTR [ 7 : 4 ] == \"0110\" @[ 751 , 526 , 135 , 21 ]\n;\nREADMEM -> BUMPN when INSTR [ 7 : 4 ] == \"0111\" @[ 797 , 492 , 135 , 21 ]\n;\nREADMEM -> COPYFROM when INSTR [ 7 : 4 ] == \"0010\" @[ 569 , 550 , 135 , 21 ]\n;\nREADMEM -> ADD when INSTR [ 7 : 4 ] == \"0100\" @[ 599 , 578 , 135 , 21 ]\n;\nREADMEM -> HALT when default @[ 575 , 429 , 47 , 21 ]\n;\nREADMEM -> SUB when INSTR [ 7 : 4 ] == \"0101\" @[ 639 , 604 , 135 , 21 ]\n;\n}\n}\nstate COPYFROM = \"010000\" @[ 555 , 622 , 30 , 30 ]\n{\ncommands @[ 490 , 662 , 75 , 36 ]\n{\nmuxR = \"01\" ;\nwR = \"1\" ;\n}\ntransitions {\nCOPYFROM -> Inc_PC when default @[ 85 , 624 , 47 , 21 ]\n;\n}\n}\nstate DECODE = \"010010\" @[ 347 , 256 , 30 , 30 ]\n{\ncommands @[ 392 , 271 , 30 , 20 ]\n{\n}\ntransitions {\nDECODE -> OUTBOX when INSTR [ 7 : 4 ] == \"0001\" . outFull == \"0\" @[ 172 , 359 ,\n232 , 21 ]\n;\nDECODE -> INBOX1 when INSTR [ 7 : 4 ] == \"0000\" . inEmpty == \"0\" @[ 257 , 385 ,\n241 , 21 ]\n;\nDECODE -> HALT when INSTR [ 7 : 4 ] == \"1111\" @[ 380 , 410 , 135 , 21 ]\n;\nDECODE -> INCPC2 when default @[ 487 , 230 , 47 , 21 ]\n;\nDECODE -> WAIT_INBOX when INSTR [ 7 : 4 ] == \"0000\" . inEmpty == \"1\" @[ 407 ,\n309 , 241 , 21 ]\n;\nDECODE -> WAIT_OUTBOX when INSTR [ 7 : 4 ] == \"0001\" . outFull == \"1\" @[ 125 ,\n257 , 232 , 21 ]\n;\n}\n}\nstate HALT = \"010100\" @[ 483 , 444 , 30 , 30 ]\n{\ncommands @[ 528 , 459 , 57 , 21 ]\n{\nhalt = \"1\" ;\n}\n}\nstate COPYTO = \"010110\" @[ 1298 , 753 , 30 , 30 ]\n{\ncommands @[ 1329 , 805 , 54 , 21 ]\n{\nwM = \"1\" ;\n}\ntransitions {\nCOPYTO -> Inc_PC when default @[ 69 , 696 , 47 , 21 ]\n;\n}\n}\nstate JUMP = \"011000\" @[ 818 , 138 , 30 , 30 ]\n{\ncommands @[ 847 , 186 , 76 , 51 ]\n{\nbranch = \"1\" ;\nijump = \"1\" ;\nwPC = \"1\" ;\n}\ntransitions {\nJUMP -> FETCH_I when default @[ 679 , 111 , 47 , 21 ]\n;\n}\n}\nstate LOAD_IR = \"011010\" @[ 351 , 156 , 30 , 30 ]\n{\ncommands @[ 411 , 171 , 55 , 21 ]\n{\nwIR = \"1\" ;\n}\ntransitions {\nLOAD_IR -> DECODE when default @[ 331 , 215 , 47 , 21 ]\n;\n}\n}\nstate FETCH_O = \"011100\" @[ 651 , 305 , 30 , 30 ]\n{\ncommands @[ 711 , 341 , 30 , 20 ]\n{\n}\ntransitions {\nFETCH_O -> READMEM when default @[ 663 , 374 , 47 , 21 ]\n;\nFETCH_O -> JUMP when INSTR [ 7 : 4 ] == \"1000\" @[ 731 , 256 , 135 , 21 ]\n;\nFETCH_O -> COPYTO when INSTR [ 7 : 4 ] == \"0011\" @[ 1225 , 431 , 135 , 21 ]\n;\nFETCH_O -> JUMPZ when INSTR [ 7 : 4 ] == \"1001\" @[ 804 , 285 , 135 , 21 ]\n;\nFETCH_O -> JUMPN when INSTR [ 7 : 4 ] == \"1010\" @[ 916 , 311 , 135 , 21 ]\n;\n}\n}\nstate ADD = \"011110\" @[ 621 , 682 , 30 , 30 ]\n{\ncommands @[ 605 , 733 , 84 , 51 ]\n{\nmuxR = \"11\" ;\naluCtl = \"000\" ;\nwR = \"1\" ;\n}\ntransitions {\nADD -> Inc_PC when default @[ 91 , 670 , 47 , 21 ]\n;\n}\n}\nstate SUB = \"100000\" @[ 709 , 680 , 30 , 30 ]\n{\ncommands @[ 702 , 734 , 84 , 51 ]\n{\nmuxR = \"11\" ;\naluCtl = \"001\" ;\nwR = \"1\" ;\n}\ntransitions {\nSUB -> Inc_PC when default @[ 55 , 723 , 47 , 21 ]\n;\n}\n}\nstate WAIT_INBOX = \"100010\" @[ 536 , 332 , 30 , 30 ]\n{\ncommands @[ 581 , 347 , 30 , 20 ]\n{\n}\ntransitions {\nWAIT_INBOX -> DECODE when default @[ 449 , 336 , 47 , 21 ]\n;\n}\n}\nstate JUMPZ = \"100100\" @[ 932 , 134 , 30 , 30 ]\n{\ncommands @[ 956 , 184 , 84 , 66 ]\n{\nbranch = \"1\" ;\nijump = \"0\" ;\naluCtl = \"000\" ;\nwPC = \"1\" ;\n}\ntransitions {\nJUMPZ -> FETCH_I when default @[ 736 , 88 , 47 , 21 ]\n;\n}\n}\nstate JUMPN = \"100110\" @[ 1043 , 136 , 30 , 30 ]\n{\ncommands @[ 1069 , 185 , 84 , 66 ]\n{\nbranch = \"1\" ;\nijump = \"0\" ;\naluCtl = \"100\" ;\nwPC = \"1\" ;\n}\ntransitions {\nJUMPN -> FETCH_I when default @[ 801 , 69 , 47 , 21 ]\n;\n}\n}\nstate BUMPP = \"101000\" @[ 850 , 622 , 30 , 30 ]\n{\ncommands @[ 840 , 672 , 84 , 51 ]\n{\nmuxR = \"11\" ;\naluCtl = \"010\" ;\nwR = \"1\" ;\n}\ntransitions {\nBUMPP -> COPYTO when default @[ 1035 , 712 , 47 , 21 ]\n;\n}\n}\nstate BUMPN = \"101010\" @[ 917 , 566 , 30 , 30 ]\n{\ncommands @[ 928 , 618 , 84 , 51 ]\n{\nmuxR = \"11\" ;\naluCtl = \"011\" ;\nwR = \"1\" ;\n}\ntransitions {\nBUMPN -> COPYTO when default @[ 1172 , 678 , 47 , 21 ]\n;\n}\n}\nstate WAIT_OUTBOX = \"101100\" @[ 191 , 285 , 30 , 30 ]\n{\ncommands @[ 179 , 331 , 30 , 20 ]\n{\n}\ntransitions {\nWAIT_OUTBOX -> DECODE when default @[ 269 , 317 , 47 , 21 ]\n;\n}\n}\n}")) ControlUnit: pin names not known; wires that end beside it: clock_1_out, rst, 1'b1, INSTR, empty, full, wIR, muxR, wR, muxM, srcA, wM, fb, aluCtl, wPC, rIN, wO, ijump
  Button rstBtn (.out(rst));
  LED Halt (.in(undriven));

  // Notes on the sheet:
  //   HRM CPU
  //   @adumont
endmodule

module PC (
  input  branch,
  input  ijump,
  input  aluFlag,
  input  [7:0] jmpAddr,
  input  wPC,
  input  rst,
  output [7:0] PC
);

  wire and_1_out, clock_1_out, or_1_out, or_2_out;
  wire [7:0] adder_1_out, multiplexer_1_out, multiplexer_2_out;

  or or_1 (or_1_out, ijump, aluFlag);
  and and_1 (and_1_out, branch, or_1_out);
  Multiplexer #(.width(8), .enable("false")) multiplexer_1 (
    .in0(adder_1_out), .in1(jmpAddr), .out(multiplexer_1_out), .sel(and_1_out));
  Multiplexer #(.width(8), .enable("false")) multiplexer_2 (
    .in0(multiplexer_1_out), .in1({8{1'b0}}), .out(multiplexer_2_out), .sel(rst));
  // Probe on multiplexer_2_out
  or or_2 (or_2_out, rst, wPC);
  Register rPC (.D(multiplexer_2_out), .en(or_2_out), .clk(clock_1_out), .Q(PC));  // open: clr
  Clock clock_1 (.out(clock_1_out));
  // Probe on adder_1_out
  Adder adder_1 (.a(PC), .b(8'h1), .out(adder_1_out));  // open: cin, cout
endmodule

module INBOX (
  input  rIn,
  input  rst,
  output empty,
  output [7:0] DIN
);

  wire clock_1_out, clock_3_out, fsm_entity_1_p1, or_1_out, s1, s2;
  wire [7:0] adder_1_out, adder_2_out, inCursor_q, register_1_q, undriven;

  Clock clock_1 (.out(clock_1_out));
  // FSM_Entity #(.content("fsm InboxInit @[ 50 , 50 , 800 , 500 ]\n{ out s1 [ 1 ] @[ 829 , 99 , 21 , 15 ]\n;\nout s2 [ 1 ] @[ 829 , 137 , 21 , 15 ]\n;\ncodeWidth = 3 ; reset = S0 ; state S0 = \"000\" @[ 80 , 101 , 30 , 30 ]\n{\ncommands @[ 123 , 115 , 51 , 21 ]\n{\ns1 = \"0\" ;\n}\ntransitions {\nS0 -> S1 when default @[ 257 , 115 , 50 , 21 ]\n;\n}\n}\nstate S1 = \"010\" @[ 407 , 107 , 30 , 30 ]\n{\ncommands @[ 452 , 122 , 51 , 21 ]\n{\ns1 = \"1\" ;\n}\ntransitions {\nS1 -> S2 when default @[ 337 , 199 , 50 , 21 ]\n;\n}\n}\nstate S2 = \"100\" @[ 313 , 247 , 30 , 30 ]\n{\ncommands @[ 358 , 262 , 51 , 21 ]\n{\ns2 = \"1\" ;\n}\ntransitions {\nS2 -> S4 when default @[ 444 , 248 , 50 , 21 ]\n;\n}\n}\nstate S4 = \"001\" @[ 526 , 263 , 30 , 30 ]\n{\ncommands @[ 571 , 278 , 30 , 20 ]\n{\n}\n}\n}")) fsm_entity_1: pin names not known; wires that end beside it: fsm_entity_1_p1, rst, 1'b1, s1, s2
  Clock clock_2 (.out(fsm_entity_1_p1));
  or or_1 (or_1_out, rIn, s2);
  Register inCursor (.D(adder_1_out), .en(or_1_out), .clk(clock_1_out), .Q(inCursor_q), .clr(rst));
  ROM rom_1 (.addr(inCursor_q));  // open: data
  Adder adder_1 (.a(inCursor_q), .b(8'h1), .out(adder_1_out));  // open: cin, cout
  Register register_1 (.D(DIN), .en(s1), .clk(clock_1_out), .Q(register_1_q), .clr(rst));
  Adder adder_2 (.a(register_1_q), .b(8'h1), .out(adder_2_out));  // open: cin, cout
  Clock clock_3 (.out(clock_3_out));
  Register inboxData (.D(undriven), .en(1'b1), .clk(clock_3_out), .Q(DIN), .clr(rst));
  Comparator comparator_1 (.a(inCursor_q), .b(adder_2_out), .eq(empty));  // open: gt, lt
endmodule

module IR (
  input  [7:0] nIR,
  input  wIR,
  output [7:0] rIR
);

  wire clock_1_out;

  Register register_1 (.D(nIR), .en(wIR), .clk(clock_1_out), .Q(rIR));  // open: clr
  Clock clock_1 (.out(clock_1_out));
endmodule

module R (
  input  [7:0] iInbox,
  input  [7:0] iMem,
  input  [7:0] iAlu,
  input  [1:0] muxR,
  input  wR,
  output [7:0] R
);

  wire clock_1_out;
  wire [7:0] multiplexer_1_out;

  Multiplexer #(.select(2), .width(8), .enable("false")) multiplexer_1 (
    .in0(iInbox), .in1(iMem), .in3(iAlu), .out(multiplexer_1_out), .sel(muxR));  // open: in2
  Register register_1 (.D(multiplexer_1_out), .en(wR), .clk(clock_1_out), .Q(R));  // open: clr
  Clock clock_1 (.out(clock_1_out));
endmodule

module OUTBOX (
  input  [7:0] DOUT,
  input  wO,
  output full
);

  wire clock_1_out, clock_2_out;
  wire [5:0] adder_1_out, register_1_q;

  Clock clock_1 (.out(clock_1_out));
  Register #(.width(6)) register_1 (.D(adder_1_out), .en(wO), .clk(clock_1_out), .Q(register_1_q));  // open: clr
  Adder #(.width(6)) adder_1 (.a(register_1_q), .b(6'b000001), .out(adder_1_out));  // open: cin, cout
  // RAM #(.addrWidth(6)) ram_1: pin names not known; wires that end beside it: register_1_q, DOUT
  Clock clock_2 (.out(clock_2_out));
  Comparator #(.width(6), .mode("unsigned")) comparator_1 (.a(register_1_q), .b({6{1'b1}}), .eq(full));  // open: gt, lt
endmodule

module MEMORY (
  input  [7:0] ADDR,
  input  srcA,
  input  wM,
  input  [7:0] R,
  input  [7:0] aluOut,
  input  muxM,
  input  fb,
  output [7:0] M
);

  wire clock_1_out, clock_2_out;
  wire [7:0] indirectFeedback_q, multiplexer_1_out, multiplexer_2_out;

  Register indirectFeedback (.D(M), .en(fb), .clk(clock_1_out), .Q(indirectFeedback_q));  // open: clr
  Clock clock_1 (.out(clock_1_out));
  Multiplexer #(.width(8), .enable("false")) multiplexer_1 (
    .in0(ADDR), .in1(indirectFeedback_q), .out(multiplexer_1_out), .sel(srcA));
  Clock clock_2 (.out(clock_2_out));
  Multiplexer #(.width(8), .enable("false")) multiplexer_2 (.in0(R), .in1(aluOut), .out(multiplexer_2_out), .sel(muxM));
  // Probe on multiplexer_1_out
  // RAM #(.databus("bibus")) ram_1: pin names not known; wires that end beside it: multiplexer_1_out, wM
  // Probe on multiplexer_2_out

  // Notes on the sheet:
  //   Select Value Input
  //   contents of ram_1 (hex, n*v repeats v):
  //   4*0 1 3
endmodule

module ALU (
  input  [7:0] inR,
  input  [7:0] inM,
  input  [2:0] aluCtl,
  output flag,
  output [7:0] aluOut
);

  wire comparator_1_eq, comparator_1_lt;
  wire [7:0] adder_1_out, adder_2_out, multiplexer_2_out, multiplexer_3_out, subtractor_1_out,
       subtractor_2_out;

  // Probe on inR
  // Probe on inM
  Comparator comparator_1 (.a(inR), .b({8{1'b0}}), .eq(comparator_1_eq), .lt(comparator_1_lt));  // open: gt
  Adder adder_1 (.a(inR), .b(inM), .out(adder_1_out));  // open: cin, cout
  Subtractor subtractor_1 (.a(inR), .b(inM), .out(subtractor_1_out));  // open: bin, bout
  Adder adder_2 (.a(inM), .b(8'h1), .out(adder_2_out));  // open: cin, cout
  Subtractor subtractor_2 (.a(inM), .b(8'h1), .out(subtractor_2_out));  // open: bin, bout
  Multiplexer #(.enable("false")) multiplexer_1 (
    .in0(comparator_1_eq), .in1(comparator_1_lt), .out(flag), .sel(aluCtl[2]));
  Multiplexer #(.width(8), .enable("false")) multiplexer_2 (
    .in0(adder_1_out), .in1(subtractor_1_out), .out(multiplexer_2_out), .sel(aluCtl[0]));
  Multiplexer #(.width(8), .enable("false")) multiplexer_3 (
    .in0(adder_2_out), .in1(subtractor_2_out), .out(multiplexer_3_out), .sel(aluCtl[0]));
  Multiplexer #(.width(8), .enable("false")) multiplexer_4 (
    .in0(multiplexer_2_out), .in1(multiplexer_3_out), .out(aluOut), .sel(aluCtl[1]));
endmodule

module tmp (
  input  in_1,
  input  in_2,
  input  [1:0] muxR,
  input  in_4,
  input  in_5,
  input  in_6,
  input  in_7,
  input  in_8,
  input  ijump,
  input  [2:0] aluCtl,
  input  in_11,
  input  in_12,
  input  wPC,
  input  [2:0] in_14,
  input  wO,
  output [3:0] out_16
);

  wire clock_1_out;

  Clock clock_1 (.out(clock_1_out));
  // FSM_Entity #(.content("fsm example @[ 50 , 50 , 800 , 500 ]\n{ in A [ 3 ] @[ 50 , 100 , 44 , 15 ]\n;\nout X [ 4 ] @[ 807 , 140 , 43 , 15 ]\n;\ncodeWidth = 2 ; reset = S0 ; state S0 = \"00\" @[ 249 , 171 , 30 , 30 ]\n{\ncommands @[ 294 , 186 , 67 , 21 ]\n{\nX = \"0001\" ;\n}\ntransitions {\nS0 -> S1 when default @[ 372 , 148 , 50 , 21 ]\n;\nS0 -> S3 when A == \"000\" @[ 346 , 269 , 78 , 21 ]\n;\n}\n}\nstate S1 = \"10\" @[ 467 , 146 , 30 , 30 ]\n{\ncommands @[ 512 , 161 , 67 , 21 ]\n{\nX = \"0010\" ;\n}\ntransitions {\nS1 -> S2 when default @[ 533 , 276 , 50 , 21 ]\n;\nS1 -> S0 when A == \"000\" @[ 376 , 216 , 78 , 21 ]\n;\n}\n}\nstate S2 = \"00\" @[ 471 , 339 , 30 , 30 ]\n{\ncommands @[ 543 , 353 , 131 , 21 ]\n{\nX = { \"00\" , A [ 1 : 0 ] , \"1\" } ;\n}\ntransitions {\nS2 -> S3 when default @[ 392 , 398 , 50 , 21 ]\n;\nS2 -> S1 when A [ 2 : 1 ] == \"11\" @[ 557 , 250 , 100 , 21 ]\n;\n}\n}\nstate S3 = \"10\" @[ 265 , 329 , 30 , 30 ]\n{\ncommands @[ 310 , 344 , 67 , 21 ]\n{\nX = \"1000\" ;\n}\ntransitions {\nS3 -> S0 when default @[ 248 , 278 , 50 , 21 ]\n;\nS3 -> S2 when A == \"000\" @[ 388 , 313 , 78 , 21 ]\n;\n}\n}\n}")) fsm_entity_1: pin names not known; wires that end beside it: clock_1_out, in_11, in_12, in_14, out_16

  // Other names for the same wires on the sheet: branch = in_8; muxM = in_4; rIN = in_2; srcA = in_5; wIR = in_1;
  //   wM = in_7; wR = in_6
endmodule

module PROG (
  input  [7:0] Addr,
  output [7:0] Data
);

  wire clock_1_out;
  wire [7:0] undriven;

  ROM rom_1 (.addr(Addr));  // open: data
  Register register_1 (.D(undriven), .en(1'b1), .clk(clock_1_out), .Q(Data), .clr(1'b0));
  Clock clock_1 (.out(clock_1_out));

  // Notes on the sheet:
  //   contents of rom_1 (hex, n*v repeats v):
  //   20 4 40 5 60 5 10 f0
endmodule
